# Fritzing sketch esquematico rs485_shieldUfox_sonda_nivel (saved by Fritzing 0.9.3b)

parts:
  RS485_module1 = RS485 Module (MAX3485)
  JP1 = Header 4 [package=1x04-smd]
  ufox1 = UFOX BOARD V1.2.6 [package=THT]  # not connected
  Componente1 = Lithium Ion Cylindrical Battery 3.7v 2200mAh [part_number=1781]
  Shield_Ufox_1 = Shield Ufox V1.1 [form="♀ (female)" package=THT]
  Solar_Cell1 = 5V 100mA Polycrystalline PET Solar Cell [part_number=IM130407002]  # not connected
  U1 = DC 5V TO ± 12V Mini DC converter [package=THT]
  Q1 = NPN-Transistor [package="TO92 [THT]"]  # not connected
  R1 = Resistor [tolerance=±5% resistance=220 package="1206 [SMD]"]

nets:
  GND: RS485_module1.GND, JP1.4, Shield_Ufox_1.pin_108, Shield_Ufox_1.pin_109, U1.GND
  N1: RS485_module1.A, JP1.2
  N2: RS485_module1.B, JP1.3
  N3: RS485_module1.VCC, Shield_Ufox_1.pin_19
  N4: RS485_module1.RO, Shield_Ufox_1.pin_12
  N5: RS485_module1.RE, RS485_module1.DE, Shield_Ufox_1.pin_14
  N6: RS485_module1.DI, Shield_Ufox_1.pin_11
  N7: JP1.1, U1.-12V
  N8: Componente1.positive, Shield_Ufox_1.pin_36
  N9: Componente1.negative, Shield_Ufox_1.pin_35
  N10: Shield_Ufox_1.pin_47, Shield_Ufox_1.pin_100, Shield_Ufox_1.pin_101
  N11: Shield_Ufox_1.pin_58, U1.Vin
  N12: Shield_Ufox_1.pin_98, Shield_Ufox_1.pin_120, R1.Pin_1
  N13: Shield_Ufox_1.pin_104, R1.Pin_0

notes:
  Lectura de RS485 Modbus - Ufox Sigfox
  Booster DC: 3 a 12V MT3608
  RS485 Sonda de nivel de agua HDL300
  +V
  A
  B
  GND
  MAX485-
  Modulo
  Transistor 2N2222A como switch
  Panel Solar 9V 3W

custom parts:
  RS485 Module (MAX3485): Commercially available RS485 to RS232 TTL Module
  UFOX BOARD V1.2.6: Kit de desarrollo Sigfox - TECA
  Lithium Ion Cylindrical Battery 3.7v 2200mAh: This lithium ion battery has a capacity of 2200mAh and a protection circuit that provides over-voltage, under-voltage and over-current protection. This cell can provide 2C of peak current (4400mA). Note that these batteries are not designed to sustain such high loads, we suggest keeping any constant current draw under about 0.5C (1 Amp).
  Shield Ufox V1.1: Shield Ufox
  5V 100mA Polycrystalline PET Solar Cell: This is 5V 100mA Polycrystalline PET Solar Cell. It is high quality and exquisite appearance. It is used in all kinds of high-grade electronic products.
  DC 5V TO ± 12V Mini DC converter: DC 5V TO ± 12V Mini DC converter from ebay (search for "DC 5V TO ± 12V Mini DC converter"). Supplies ± 12V at up to 30MA output for op amps or rs232 drivers from a 3 to 5V input (so a battery or 3.3 or 5V power rail) on a micro).
